// Logisim project cpu01.circ as structural Verilog: 4 circuits, main circuit main
module main (
);

  wire K0, K1, K2, K3, L0, L1, L2, L3, L4, L5, L6, L7, L8, L9, S0, S1, S2, S3, S4, S5, S6, S7, S8, S9;
  wire [3:0] HEX0, HEX1, HEX2, HEX3, HEX4, HEX5;

  Hex_Digit_Display hex_digit_display_1 (.value(HEX5));  // open: dp
  LED u_L8 (.in(L8));
  LED u_L9 (.in(L9));
  // DipSwitch #(.NSwitches(1)) S8: pin names not known; wires that end beside it: S8
  // DipSwitch #(.NSwitches(1)) S9: pin names not known; wires that end beside it: S9
  Hex_Digit_Display hex_digit_display_2 (.value(HEX3));  // open: dp
  Hex_Digit_Display hex_digit_display_3 (.value(HEX4));  // open: dp
  LED u_L6 (.in(L6));
  LED u_L7 (.in(L7));
  LED u_L5 (.in(L5));
  // DipSwitch #(.NSwitches(1)) S6: pin names not known; wires that end beside it: S6
  // DipSwitch #(.NSwitches(1)) S7: pin names not known; wires that end beside it: S7
  // DipSwitch #(.NSwitches(1)) S5: pin names not known; wires that end beside it: S5
  Hex_Digit_Display hex_digit_display_4 (.value(HEX2));  // open: dp
  LED u_L3 (.in(L3));
  LED u_L4 (.in(L4));
  // DipSwitch #(.NSwitches(1)) S4: pin names not known; wires that end beside it: S4
  // DipSwitch #(.NSwitches(1)) S2: pin names not known; wires that end beside it: S2
  // DipSwitch #(.NSwitches(1)) S3: pin names not known; wires that end beside it: S3
  Hex_Digit_Display hex_digit_display_5 (.value(HEX0));  // open: dp
  Hex_Digit_Display hex_digit_display_6 (.value(HEX1));  // open: dp
  LED u_L0 (.in(L0));
  LED u_L2 (.in(L2));
  LED u_L1 (.in(L1));
  // DipSwitch #(.NSwitches(1)) S0: pin names not known; wires that end beside it: S0
  // DipSwitch #(.NSwitches(1)) S1: pin names not known; wires that end beside it: S1
  Button u_K3 (.out(K3));
  Button u_K2 (.out(K2));
  Button u_K0 (.out(K0));
  Button u_K1 (.out(K1));
  registrador_1 registrador_1_1 (
    .in_1(S9), .out_6(HEX0[0]), .out_7(HEX0[1]), .out_8(HEX0[2]), .out_9(HEX0[3]), .D0(S1), .in_3(S2),
    .in_4(S3), .in_5(S4));
  contador_sinc_8 contador_sinc_8_1 (
    .JMP(HEX4[3:2]), .OP(HEX2), .CLOCK(S9), .CLEAR(S0), .Q0(L0), .Q1(L1), .Q2(L2), .Q3(L3), .Q4(L4), .Q5(L5),
    .Q6(L6), .Q7(L7));
  ROM #(.dataWidth(16), .Select("low")) rom_1 (
    .addr({L7, L6, L5, L4, L3, L2, L1, L0}), .data({HEX5, HEX4, HEX3, HEX2}));
  ula ula_1 (.in_1(HEX4[1:0]));  // open: in_2, in_3, in_4, in_5, in_6, in_7, in_8, in_9, out_14, out_10, out_12, out_11, out_13

  // Notes on the sheet:
  //   contents of rom_1 (hex, n*v repeats v):
  //   110 0 0 101 1001 1 0 1 110 10 0 10 110 11 0 100 0 1100 0 1000 13*0 100 0 0 110 0 0 1 1001 0 0 1 1001
  //   0 0 10 110 11 0 10 110 1 0 10 1001 11 0 10 110 10 0 0 110 0 0 1 0 1000
endmodule

module contador_sinc_8 (
  input  CLOCK,
  input  CLEAR,
  input  [1:0] JMP,
  input  [3:0] OP,
  output Q0,
  output Q1,
  output Q2,
  output Q3,
  output Q4,
  output Q5,
  output Q6,
  output Q7
);

  wire and_1_out, and_2_out, and_3_out, and_4_out, and_5_out, and_6_out, and_7_out, and_8_out, and_9_out,
       and_10_out, and_11_out, and_12_out, and_13_out, and_14_out, nand_1_out, nand_2_out, nand_3_out,
       nand_4_out, not_1_out, not_2_out, not_3_out, not_4_out, not_5_out, not_6_out, not_7_out, not_8_out,
       or_1_out, or_2_out, or_3_out, or_4_out;

  nand nand_1 (nand_1_out, OP[0], JMP[0]);
  or or_1 (or_1_out, OP[0], not_1_out);
  not not_1 (not_1_out, JMP[0]);
  T_Flip_Flop #(.NegatePresetClear("true")) t_ff_1 (
    .clk(CLOCK), .T(1'b1), .Q(Q0), .preset(nand_1_out), .reset(and_1_out));  // open: Qn
  and and_1 (and_1_out, or_1_out, CLEAR);
  nand nand_2 (nand_2_out, OP[1], JMP[0]);
  and and_2 (and_2_out, or_2_out, CLEAR);
  or or_2 (or_2_out, OP[1], not_2_out);
  not not_2 (not_2_out, JMP[0]);
  T_Flip_Flop #(.NegatePresetClear("true")) t_ff_2 (
    .clk(CLOCK), .T(Q0), .Q(Q1), .preset(nand_2_out), .reset(and_2_out));  // open: Qn
  nand nand_3 (nand_3_out, OP[2], JMP[0]);
  and and_3 (and_3_out, Q0, Q1);
  and and_4 (and_4_out, or_3_out, CLEAR);
  or or_3 (or_3_out, OP[2], not_3_out);
  not not_3 (not_3_out, JMP[0]);
  T_Flip_Flop #(.NegatePresetClear("true")) t_ff_3 (
    .clk(CLOCK), .T(and_3_out), .Q(Q2), .preset(nand_3_out), .reset(and_4_out));  // open: Qn
  and and_5 (and_5_out, Q2, Q0, Q1);
  or or_4 (or_4_out, OP[3], not_4_out);
  not not_4 (not_4_out, JMP[0]);
  nand nand_4 (nand_4_out, OP[3], JMP[0]);
  T_Flip_Flop #(.NegatePresetClear("true")) t_ff_4 (
    .clk(CLOCK), .T(and_5_out), .Q(Q3), .preset(nand_4_out), .reset(and_6_out));  // open: Qn
  and and_6 (and_6_out, or_4_out, CLEAR);
  and and_7 (and_7_out, Q3, Q0, Q1, Q2);
  and and_8 (and_8_out, not_5_out, CLEAR);
  not not_5 (not_5_out, JMP[0]);
  T_Flip_Flop #(.NegatePresetClear("true")) t_ff_5 (
    .clk(CLOCK), .T(and_7_out), .Q(Q4), .preset(1'b1), .reset(and_8_out));  // open: Qn
  and and_9 (and_9_out, Q4, Q0, Q1, Q2, Q3);
  and and_10 (and_10_out, not_6_out, CLEAR);
  not not_6 (not_6_out, JMP[0]);
  T_Flip_Flop #(.NegatePresetClear("true")) t_ff_6 (
    .clk(CLOCK), .T(and_9_out), .Q(Q5), .preset(1'b1), .reset(and_10_out));  // open: Qn
  and and_11 (and_11_out, Q5, Q0, Q1, Q2, Q3, Q4);
  T_Flip_Flop #(.NegatePresetClear("true")) t_ff_7 (
    .clk(CLOCK), .T(and_11_out), .Q(Q6), .preset(1'b1), .reset(and_12_out));  // open: Qn
  and and_12 (and_12_out, not_7_out, CLEAR);
  not not_7 (not_7_out, JMP[0]);
  T_Flip_Flop #(.NegatePresetClear("true")) t_ff_8 (
    .clk(CLOCK), .T(and_13_out), .Q(Q7), .preset(1'b1), .reset(and_14_out));  // open: Qn
  and and_13 (and_13_out, Q6, Q0, Q1, Q2, Q3, Q4, Q5);
  and and_14 (and_14_out, not_8_out, CLEAR);
  not not_8 (not_8_out, JMP[0]);
endmodule

module registrador_1 (
  input  in_1,
  input  D0,
  input  in_3,
  input  in_4,
  input  in_5,
  output out_6,
  output out_7,
  output out_8,
  output out_9
);

  D_Flip_Flop #(.trigger("falling")) d_ff_1 (.clk(in_1), .D(D0), .Q(out_6));  // open: Qn, preset, reset
  D_Flip_Flop #(.trigger("falling")) d_ff_2 (.clk(in_1), .D(in_3), .Q(out_7));  // open: Qn, preset, reset
  D_Flip_Flop #(.trigger("falling")) d_ff_3 (.clk(in_1), .D(in_4), .Q(out_8));  // open: Qn, preset, reset
  D_Flip_Flop #(.trigger("falling")) d_ff_4 (.clk(in_1), .D(in_5), .Q(out_9));  // open: Qn, preset, reset

  // Other names for the same wires on the sheet: CLOCK = in_1
endmodule

module ula (
  input  [1:0] in_1,
  input  in_2,
  input  in_3,
  input  in_4,
  input  in_5,
  input  in_6,
  input  in_7,
  input  in_8,
  input  in_9,
  output out_10,
  output out_11,
  output out_12,
  output out_13,
  output out_14
);

  wire nand_1_out;
  wire [3:0] SaidaDiv, SaidaMult, SaidaSoma, SaidaSub;

  nand nand_1 (nand_1_out, in_1[0], in_1[1]);
  Subtractor #(.width(4)) subtractor_1 (
    .a({in_5, in_4, in_3, in_2}), .b({in_9, in_8, in_7, in_6}), .out(SaidaSub));  // open: bin, bout
  Adder #(.width(4)) adder_1 (
    .a({in_5, in_4, in_3, in_2}), .b({in_9, in_8, in_7, in_6}), .out(SaidaSoma), .cout(out_14));  // open: cin
  Multiplier #(.width(4)) multiplier_1 (.a({in_5, in_4, in_3, in_2}), .b(4'b0010), .out(SaidaMult));  // open: cin, cout
  Divider #(.width(4)) divider_1 (.a({in_5, in_4, in_3, in_2}), .b(4'b0010), .out(SaidaDiv));  // open: upper, rem
  Hex_Digit_Display hex_digit_display_1 (.value(SaidaSoma));  // open: dp
  Hex_Digit_Display hex_digit_display_2 (.value(SaidaSub));  // open: dp
  Hex_Digit_Display hex_digit_display_3 (.value(SaidaMult));  // open: dp
  Hex_Digit_Display hex_digit_display_4 (.value(SaidaDiv));  // open: dp

  // Other names for the same wires on the sheet: R1[3:0] = {in_5, in_4, in_3, in_2};
  //   R2[3:0] = {in_9, in_8, in_7, in_6}; Saida[3:0] = {out_13, out_12, out_11, out_10}
endmodule
